# Fritzing sketch sketch (saved by Fritzing 0.9.3b)
breadboards: 1

parts:
  Componente1 = Arduino Uno (Rev3) - ICSP
  LCD1 = LCD screen
  U1 = RELAY [package=OJ]
  DHT1 = DHT11 Humitidy and Temperature Sensor
  LED1 = LED - 5mm [color="Red (633nm)" package="5 mm [THT]"]
  U2 = POT [package=pot_mammoth]
  U3 = POT [package=pot_mammoth]

nets:
  N1: Componente1.A0, U2.A
  N2: Componente1.A1, U3.A
  N3: Componente1.D8, LCD1.E
  N4: Componente1.D9_PWM, LCD1.DB4
  N5: Componente1.D10_PWM/SS, LCD1.DB5
  N6: Componente1.D11_PWM/MOSI, LCD1.DB6
  N7: Componente1.D12/MISO, LCD1.DB7
  N8: Componente1.D2, DHT1.DATA
  N9: Componente1.D3_PWM, U1.MAIN
  N10: Componente1.D4, LED1.anode
  N11: Componente1.D7, LCD1.RS
  VDD: Componente1.5V, LCD1.VDD, DHT1.VDD, U2.S, U3.S
  GND: Componente1.GND, LCD1.VSS, LCD1.R/W, U1.NO, DHT1.GND, LED1.cathode, U2.E, U3.E

custom parts:
  DHT11 Humitidy and Temperature Sensor: DHT11 Humidity and Temperature Sensor

// code stored in the sketch: source_arduino.ino
#include <LiquidCrystal.h>
LiquidCrystal lcd(7, 8, 9, 10, 11 , 12); 
#include "DHT.h"
#define DHTPIN 2 
#define DHTTYPE DHT11
const int rele=3, led=4;
long varPot, varPot2;
DHT dht(DHTPIN, DHTTYPE);

void setup(){
  Serial.begin(9600);
  Serial.println("Prueba DHT11");
  pinMode(rele,OUTPUT);
  pinMode(led,OUTPUT);
  dht.begin();
  lcd.begin(16,2);
  lcd.setCursor(0,0); 
  lcd.write("Espere...."); 
  }

void loop(){
  delay(2000);
  varPot = analogRead(A0);
  varPot2= analogRead(A1);
  varPot2=varPot2/20;
  varPot=varPot/20;
  float h = dht.readHumidity();
  float t = dht.readTemperature();
  if (isnan(h) || isnan(t)) {
    Serial.println("Esperando DHT11...");
    return;
  }
  
    if(t<=varPot2){
      //Activa relé
      digitalWrite(rele,HIGH);
      digitalWrite(led,HIGH);
    }
    else if(t>=varPot){
      digitalWrite(rele,LOW);
      digitalWrite(led,LOW);
    }
    
  lcd.begin(16, 2); 
  lcd.setCursor(0,0); 
  lcd.write("Temperatura: "); 
  lcd.setCursor(12,0); 
  lcd.print(t);
  lcd.setCursor(14,0); 
  lcd.write((char)223);
  lcd.setCursor(15,0); 
  lcd.write("C");
  
  lcd.setCursor(0,1); 
  //lcd.write("Humedad: ");
  lcd.write("MIN: "); 
  lcd.setCursor(4,1); 
  //lcd.print(h);
  lcd.print(varPot);
  lcd.setCursor(8,1);
  lcd.print("MAX: ");
  lcd.print(varPot2);
  lcd.setCursor(14,1);
  //lcd.write("%");
}
